# Fritzing sketch Simple Example (saved by Fritzing 0.7.12b)

parts:
  Arduino1 = Arduino
  EDGY_motor_control1 = EDGY
  M1 = DC Motor
  J1 = Basic Force Sensing Resistor (FSR) [package=THT]
  R1 = 470 Ω Resistor [package=THT]
  S4 = Round Pushbutton
  Part2 = Ambient Light Sensor (TEMT6000 Breakout Board)
  Nano1 = Arduino Nano v3.0
  R2 = Basic Photo-Resistor (Photocell) [package=THT]  # not connected
  M2 = DC Motor

nets:
  N1: Arduino1.GND, J1.pin_0
  N2: Arduino1.D13, S4.leg1
  N3: Arduino1.D8, EDGY_motor_control1.A1
  N4: Arduino1.D7, EDGY_motor_control1.B1
  N5: Arduino1.D6, EDGY_motor_control1.Speed1
  N6: Arduino1.+5V, R1.Pin_0, S4.leg0
  N7: Arduino1.A0, J1.pin_1, R1.Pin_1
  N8: Arduino1.A4, Nano1.A4
  N9: Arduino1.A5, Nano1.A5
  N10: EDGY_motor_control1.B2, Nano1.D7
  N11: EDGY_motor_control1.Speed2, Nano1.D11
  N12: EDGY_motor_control1.B2out, M2.pin_2
  N13: EDGY_motor_control1.A2out, M2.pin_1
  N14: EDGY_motor_control1.B1out, M1.pin_2
  N15: EDGY_motor_control1.A1out, M1.pin_1
  VCC: Part2.VCC, Nano1.+5V
  GND: Part2.GND, Nano1.GND
  N16: Part2.S, Nano1.A7
